# Fritzing sketch SN54HC164 (saved by Fritzing 0.9.3b)
circuit board: 8.46667cm x 5.64444cm
breadboards: 1

parts:
  U1 = atmega328 [package=dip]
  R1 = Resistor [tolerance=±5% resistance=220 package=THT]
  R2 = Resistor [tolerance=±5% resistance=220 package=THT]
  R3 = Resistor [tolerance=±5% resistance=220 package=THT]
  R4 = Resistor [tolerance=±5% resistance=220 package=THT]
  R5 = Resistor [tolerance=±5% resistance=220 package=THT]
  R6 = Resistor [tolerance=±5% resistance=220 package=THT]
  R7 = Resistor [tolerance=±5% resistance=220 package=THT]
  R8 = Resistor [tolerance=±5% resistance=220 package=THT]
  LED1 = LED - 3mm [color="Green (560nm)" package="3 mm [THT]"]
  LED2 = LED - 3mm [color="Green (560nm)" package="3 mm [THT]"]
  LED3 = LED - 3mm [color="Green (560nm)" package="3 mm [THT]"]
  LED4 = LED - 3mm [color="Green (560nm)" package="3 mm [THT]"]
  LED5 = LED - 3mm [color="Green (560nm)" package="3 mm [THT]"]
  LED6 = LED - 3mm [color="Green (560nm)" package="3 mm [THT]"]
  LED8 = LED - 3mm [color="Green (560nm)" package="3 mm [THT]"]
  LED9 = LED - 3mm [color="Red (633nm)" package="3 mm [THT]"]
  R9 = Resistor [tolerance=±5% resistance=220 package=THT]
  LED7 = LED - 3mm [color="Green (560nm)" package="3 mm [THT]"]
  IC1 = IC, DIP package, 14 pins [chip_label=IC]
  C1 = Ceramic Capacitor [capacitance=100nF package="100 mil [THT, multilayer]"]

nets:
  N1: U1.D2, IC1.pin1, IC1.pin2
  N2: U1.D3_(PWM), IC1.pin9
  N3: U1.D4, IC1.pin8
  N4: U1.VCC, LED9.anode, IC1.pin14, C1.0
  N5: U1.GND#7, LED1.cathode, LED2.cathode, LED3.cathode, LED4.cathode, LED5.cathode, LED6.cathode, LED8.cathode, R9.Pin_1, IC1.pin7, C1.1
  N6: R1.Pin_0, LED1.anode
  N7: R1.Pin_1, IC1.pin3
  N8: R2.Pin_0, LED2.anode
  N9: R2.Pin_1, IC1.pin4
  N10: R3.Pin_0, LED3.anode
  N11: R3.Pin_1, IC1.pin5
  N12: R4.Pin_0, LED4.anode
  N13: R4.Pin_1, IC1.pin6
  N14: R5.Pin_0, LED5.anode
  N15: R5.Pin_1, IC1.pin10
  N16: R6.Pin_0, LED6.anode
  N17: R6.Pin_1, IC1.pin11
  N18: R7.Pin_0, LED7.anode
  N19: R7.Pin_1, IC1.pin12
  N20: R8.Pin_0, LED8.anode
  N21: R8.Pin_1, IC1.pin13
  N22: LED9.cathode, R9.Pin_0
